// Logisim project imm-gen.circ as structural Verilog: 1 circuit, main circuit imm_gen
module imm_gen (
  input  [31:0] inst,
  input  [2:0] ImmSel,
  output [31:0] imm
);

  wire [11:0] immediate_sb;
  wire [31:0] imm_i, imm_sb;

  assign imm = {{20{inst[31]}}, inst[31:20]};  // Bit_Extender bit_extender_1
  assign imm_sb = {{19{inst[31]}}, {inst[31], immediate_sb}};  // Bit_Extender bit_extender_2
  Multiplexer #(.enable("false"), .select(3), .width(32)) multiplexer_1 (
    .in1(imm_i), .in3(imm_sb), .out(imm), .sel(ImmSel));  // open: in0, in2, in4, in5, in6, in7

  // Other names for the same wires on the sheet: immediate[11:0] = inst[31:20]; immediate_sb[12] = inst[31]

  // Notes on the sheet:
  //   INPUTS to your circuit
  //   DON'T CHANGE THE LOCATIONS OF THE INPUTS AND OUTPUTS!
  //   OUTPUT from your circuit
endmodule
